# Fritzing sketch Servoandsensor (saved by Fritzing 0.9.3b)
breadboards: 1

parts:
  Part1 = Arduino Uno (Rev3)
  Part2 = Adafruit Bluefruit LE SPI Friend [part_number="Adafruit #2633"]  # not connected
  U3 = HC-SR04 [chip_label=IC package="SIP (Single Inline) [THT]"]
  J1 = Basic Servo

nets:
  N1: Part1.D2, J1.pulse
  VCC: U3.Vcc, J1.vcc
  GND: U3.GND, J1.gnd

custom parts:
  Adafruit Bluefruit LE SPI Friend: The Bluefruit LE SPI Friend makes it easy to add Bluetooth Low Energy connectivity to anything with 4 or 5 GPIO pins. With SPI, you don't have to worry about baud rates, flow control, or giving up a hardware UART port. Connect to your Arduino or other microcontroller using the common four-pin SPI interface (MISO, MOSI, SCK and CS) plus a 5th GPIO pin for interrupts (to let the Arduino know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
  HC-SR04: HC-SR04 ultrasound distance sensor
